// Logisim project ALU.circ as structural Verilog: 3 circuits, main circuit ALU
module ALU (
  input  [31:0] A,
  input  [31:0] B,
  input  [4:0] Shift,
  input  CarryIn,
  input  [3:0] Codop,
  output [31:0] S,
  output [3:0] Flags
);

  wire adder_2_cout, adder_3_cout, adder_4_cout, subtractor_2_out, subtractor_3_bout, subtractor_4_bout,
       xnor_1_out, xor_2_out;
  wire [31:0] adder_1_out, adder_2_out, adder_3_out, adder_4_out, and_1_out, bit_extender_1_out,
       bit_extender_2_out, multiplier_1_out, nand_1_out, not_1_out, or_1_out, shifter_1_out, shifter_2_out,
       shifter_3_out, shifter_4_out, subtractor_1_out, subtractor_3_out, subtractor_4_out, xor_1_out;

  Adder #(.width(32)) adder_1 (.a(A), .b(B), .out(adder_1_out));  // open: cin, cout
  assign bit_extender_1_out = {{31{CarryIn}}, CarryIn};  // Bit_Extender bit_extender_1
  Subtractor #(.width(32)) subtractor_1 (.a(A), .b(B), .out(subtractor_1_out));  // open: bin, bout
  Subtractor #(.width(1)) subtractor_2 (.a(CarryIn), .b(1'b1), .out(subtractor_2_out));  // open: bin, bout
  assign bit_extender_2_out = {{31{subtractor_2_out}}, subtractor_2_out};  // Bit_Extender bit_extender_2
  assign and_1_out = A & B;  // AND_Gate and_1, 32 bits wide
  assign xor_1_out = A ^ B;  // XOR_Gate xor_1, 32 bits wide
  Shifter #(.width(32)) shifter_1 (.in(B), .\dist (Shift), .out(shifter_1_out));
  Shifter #(.width(32), .shift("lr")) shifter_2 (.in(B), .\dist (Shift), .out(shifter_2_out));
  Shifter #(.width(32), .shift("ar")) shifter_3 (.in(B), .\dist (Shift), .out(shifter_3_out));
  Adder #(.width(32)) adder_2 (
    .a(adder_1_out), .b(bit_extender_1_out), .out(adder_2_out), .cout(adder_2_cout));  // open: cin
  Adder #(.width(32)) adder_3 (
    .a(subtractor_1_out), .b(bit_extender_2_out), .out(adder_3_out), .cout(adder_3_cout));  // open: cin
  Shifter #(.width(32), .shift("rr")) shifter_4 (.in(B), .\dist (Shift), .out(shifter_4_out));
  Subtractor #(.width(32)) subtractor_3 (
    .a({32{1'b0}}), .b(A), .out(subtractor_3_out), .bout(subtractor_3_bout));  // open: bin
  Subtractor #(.width(32)) subtractor_4 (.a(A), .b(B), .out(subtractor_4_out), .bout(subtractor_4_bout));  // open: bin
  Adder #(.width(32)) adder_4 (.a(A), .b(B), .out(adder_4_out), .cout(adder_4_cout));  // open: cin
  assign or_1_out = B;  // OR_Gate or_1, 32 bits wide OR_Gate
  Multiplier #(.width(32)) multiplier_1 (.a(A), .b(B), .out(multiplier_1_out));  // open: cin, cout
  assign nand_1_out = ~(A & B);  // NAND_Gate nand_1, 32 bits wide
  assign not_1_out = ~B;  // NOT_Gate not_1, 32 bits wide
  Multiplexer #(.select(4), .width(32), .enable("false")) multiplexer_1 (
    .in0(and_1_out), .in1(xor_1_out), .in2(shifter_1_out), .in3(shifter_2_out), .in4(shifter_3_out),
    .in5(adder_2_out), .in6(adder_3_out), .in7(shifter_4_out), .in9(subtractor_3_out),
    .in10(subtractor_4_out), .in11(adder_4_out), .in12(or_1_out), .in13(multiplier_1_out), .in14(nand_1_out),
    .in15(not_1_out), .out({Flags[0], S[30:0]}), .sel(Codop));  // open: in8
  Multiplexer #(.select(4), .enable("false")) multiplexer_2 (
    .in5(adder_2_cout), .in6(adder_3_cout), .in9(subtractor_3_bout), .in10(subtractor_4_bout),
    .in11(adder_4_cout), .out(Flags[2]), .sel(Codop));  // open: in0, in1, in2, in3, in4, in7, in8, in12, in13, in14, in15
  xnor xnor_1 (xnor_1_out, B[31], A[31]);
  xor xor_2 (xor_2_out, Flags[0], xnor_1_out);
  Comparator #(.width(32)) comparator_1 (.a({Flags[0], S[30:0]}), .b({32{1'b0}}), .eq(Flags[1]));  // open: gt, lt
  Multiplexer #(.select(4), .enable("false")) multiplexer_3 (
    .in5(xor_2_out), .in6(xor_2_out), .in9(xor_2_out), .in10(xor_2_out), .in11(xor_2_out), .out(Flags[3]),
    .sel(Codop));  // open: in0, in1, in2, in3, in4, in7, in8, in12, in13, in14, in15

  assign S[31] = Flags[0];

  // Other names for the same wires on the sheet: N = Flags[0]; Z = Flags[1]; C = Flags[2]; V = Flags[3]

  // Notes on the sheet:
  //   Note: for ROR, C = N
  //   Note 2: assume that shift > 0 for LSL and LSR
endmodule

module BancRegistre (
  input  Reset,
  input  [31:0] DataIn,
  input  [2:0] RegA,
  input  [2:0] RegDest,
  input  [2:0] RegB,
  input  Clk,
  output [31:0] R0,
  output [31:0] AOut,
  output [31:0] R1,
  output [31:0] R2,
  output [31:0] R3,
  output [31:0] R4,
  output [31:0] BOut,
  output [31:0] R5,
  output [31:0] R6,
  output [31:0] R7
);

  wire decoder_1_out0, decoder_1_out1, decoder_1_out2, decoder_1_out3, decoder_1_out4, decoder_1_out5,
       decoder_1_out6, decoder_1_out7;

  Decoder #(.select(3)) decoder_1 (
    .out0(decoder_1_out0), .out1(decoder_1_out1), .out2(decoder_1_out2), .out3(decoder_1_out3),
    .out4(decoder_1_out4), .out5(decoder_1_out5), .out6(decoder_1_out6), .out7(decoder_1_out7), .sel(RegDest));  // open: en
  Register #(.width(32)) register_1 (.D(DataIn), .en(decoder_1_out0), .clk(Clk), .Q(R0));  // open: clr
  Register #(.width(32)) register_2 (.D(DataIn), .en(decoder_1_out1), .clk(Clk), .Q(R1));  // open: clr
  Register #(.width(32)) register_3 (.D(DataIn), .en(decoder_1_out2), .clk(Clk), .Q(R2));  // open: clr
  Register #(.width(32)) register_4 (.D(DataIn), .en(decoder_1_out3), .clk(Clk), .Q(R3));  // open: clr
  Register #(.width(32)) register_5 (.D(DataIn), .en(decoder_1_out4), .clk(Clk), .Q(R4));  // open: clr
  Register #(.width(32)) register_6 (.D(DataIn), .en(decoder_1_out5), .clk(Clk), .Q(R5));  // open: clr
  Register #(.width(32)) register_7 (.D(DataIn), .en(decoder_1_out6), .clk(Clk), .Q(R6));  // open: clr
  Register #(.width(32)) register_8 (.D(DataIn), .en(decoder_1_out7), .clk(Clk), .Q(R7));  // open: clr
  Multiplexer #(.select(3), .width(32), .enable("false")) multiplexer_1 (
    .in0(R0), .in1(R1), .in2(R2), .in3(R3), .in4(R4), .in5(R5), .in6(R6), .in7(R7), .out(AOut), .sel(RegA));
  Multiplexer #(.select(3), .width(32), .enable("false")) multiplexer_2 (
    .in0(R0), .in1(R1), .in2(R2), .in3(R3), .in4(R4), .in5(R5), .in6(R6), .in7(R7), .out(BOut), .sel(RegB));
endmodule

module main (
  input  [31:0] in_1,
  input  [3:0] in_2
);

  wire clock_1_out;
  wire [31:0] alu_1_s, bancregistre_1_aout, bancregistre_1_bout;

  Clock clock_1 (.out(clock_1_out));
  // Probe on alu_1_s
  ALU alu_1 (
    .S(alu_1_s), .A(bancregistre_1_bout), .B(bancregistre_1_aout), .Shift({5{1'b0}}));  // open: Flags, CarryIn, Codop
  BancRegistre bancregistre_1 (
    .DataIn(in_1), .RegDest(3'b000), .Clk(clock_1_out), .AOut(bancregistre_1_aout), .BOut(bancregistre_1_bout));  // open: Reset, RegA, RegB, R0, R1, R2, R3, R4, R5, R6, R7
endmodule
