// Logisim project Controller.circ as structural Verilog: 8 circuits, main circuit Controller
module Controller (
  input  [15:0] Inst,
  input  [3:0] Flags,
  input  Clk,
  input  Reset,
  output Carry,
  output DP_Shift,
  output Imm32_Enable,
  output [4:0] Imm5,
  output [31:0] Imm32,
  output [3:0] ALU_Opcode,
  output [2:0] Rm,
  output [2:0] Rn,
  output [2:0] Rd,
  output [31:0] RAM_Addr,
  output Load,
  output Store,
  output [7:0] PC
);

  wire Conditional_1_p8, Load_Store_1_pc_hold, not_1_out, Opcode_Decoder_1_conditional,
       Opcode_Decoder_1_data_processing, Opcode_Decoder_1_load_store, Opcode_Decoder_1_shift,
       Opcode_Decoder_1_sp_address, Shift_Add_Sub_Mov_1_carry, SP_Address_1_write_enable;
  wire [2:0] Data_Processing_1_rd, Data_Processing_1_rm, Data_Processing_1_rn, Load_Store_1_rd,
       Load_Store_1_rm, Shift_Add_Sub_Mov_1_rd, Shift_Add_Sub_Mov_1_rm, Shift_Add_Sub_Mov_1_rn;
  wire [3:0] Data_Processing_1_alu_opcode, Data_Processing_1_flags_update_mask, flags_apsr_1_flags_out,
       or_1_out, Shift_Add_Sub_Mov_1_alu_opcode, Shift_Add_Sub_Mov_1_flags_update_mask;
  wire [7:0] adder_1_out, adder_2_out, Conditional_1_p7;
  wire [31:0] SP_Address_1_new_stack_pointer, Stack_Pointer_q;

  Register #(.width(32)) Stack_Pointer (
    .D(SP_Address_1_new_stack_pointer), .en(SP_Address_1_write_enable), .clk(Clk), .Q(Stack_Pointer_q),
    .clr(Reset));
  Opcode_Decoder Opcode_Decoder_1 (
    .Opcode(Inst[15:10]), .Data_Processing(Opcode_Decoder_1_data_processing), .Shift(Opcode_Decoder_1_shift),
    .Load_Store(Opcode_Decoder_1_load_store), .SP_Address(Opcode_Decoder_1_sp_address),
    .Conditional(Opcode_Decoder_1_conditional));
  assign or_1_out = Data_Processing_1_flags_update_mask | Shift_Add_Sub_Mov_1_flags_update_mask;  // OR_Gate or_1, 4 bits wide
  Shift_Add_Sub_Mov Shift_Add_Sub_Mov_1 (
    .Imm32_Enable(Imm32_Enable), .Instruction(Inst), .ALU_Opcode(Shift_Add_Sub_Mov_1_alu_opcode),
    .Enable(Opcode_Decoder_1_data_processing), .Carry(Shift_Add_Sub_Mov_1_carry),
    .Flags_Update_Mask(Shift_Add_Sub_Mov_1_flags_update_mask), .Rd(Shift_Add_Sub_Mov_1_rd),
    .Rn(Shift_Add_Sub_Mov_1_rn), .Rm(Shift_Add_Sub_Mov_1_rm), .Imm5(Imm5), .Imm32(Imm32));
  Data_Processing Data_Processing_1 (
    .Instruction(Inst), .ALU_Opcode(Data_Processing_1_alu_opcode), .Enable(Opcode_Decoder_1_shift),
    .Rm(Data_Processing_1_rm), .Rn(Data_Processing_1_rn), .Rd(Data_Processing_1_rd),
    .Flags_Update_Mask(Data_Processing_1_flags_update_mask));
  Flags_APSR flags_apsr_1 (
    .Flags_In(or_1_out), .Update_Mask(Flags), .Clk(Clk), .Rst(Reset), .Flags_Out(flags_apsr_1_flags_out));
  Load_Store Load_Store_1 (
    .Instruction(Inst), .Load(Load), .RAM_Addr(RAM_Addr), .Store(Store), .Stack_Pointer(Stack_Pointer_q),
    .Enable(Opcode_Decoder_1_load_store), .Rd(Load_Store_1_rd), .Rm(Load_Store_1_rm), .Clk(Clk),
    .Reset(Reset), .PC_Hold(Load_Store_1_pc_hold));
  // Conditional Conditional_1: pin names not known; wires that end beside it: Opcode_Decoder_1_conditional, Inst, flags_apsr_1_flags_out[3], flags_apsr_1_flags_out[2], flags_apsr_1_flags_out[1], flags_apsr_1_flags_out[0], Conditional_1_p7, Conditional_1_p8
  SP_Address SP_Address_1 (
    .New_Stack_Pointer(SP_Address_1_new_stack_pointer), .Stack_Pointer(Stack_Pointer_q),
    .Enable(Opcode_Decoder_1_sp_address), .Instruction(Inst), .Write_Enable(SP_Address_1_write_enable));
  Adder adder_1 (.a(8'h3), .b(Conditional_1_p7), .out(adder_1_out), .cin(1'b0));  // open: cout
  Adder adder_2 (.a(adder_1_out), .b(PC), .out(adder_2_out), .cin(1'b0));  // open: cout
  and and_1 (DP_Shift, Opcode_Decoder_1_data_processing, ~Opcode_Decoder_1_shift);  // AND_Gate
  not not_1 (not_1_out, Load_Store_1_pc_hold);
  Counter counter_1 (
    .clr(Reset), .load(Conditional_1_p8), .up(1'b1), .count(not_1_out), .clk(Clk), .D(adder_2_out), .Q(PC));  // open: carry
  Multiplexer #(.enable("false")) multiplexer_1 (
    .in0(flags_apsr_1_flags_out[1]), .in1(Shift_Add_Sub_Mov_1_carry), .out(Carry), .sel(DP_Shift));
  assign ALU_Opcode = Shift_Add_Sub_Mov_1_alu_opcode | Data_Processing_1_alu_opcode;  // OR_Gate or_2, 4 bits wide
  assign Rm = Shift_Add_Sub_Mov_1_rm | Data_Processing_1_rm | Load_Store_1_rm;  // OR_Gate or_3, 3 bits wide
  assign Rn = Shift_Add_Sub_Mov_1_rn | Data_Processing_1_rn;  // OR_Gate or_4, 3 bits wide
  assign Rd = Shift_Add_Sub_Mov_1_rd | Data_Processing_1_rd | Load_Store_1_rd;  // OR_Gate or_5, 3 bits wide

  // Notes on the sheet:
  //   Extract carry
  //   Extract Opcode
  //   IF Reg_Imm=1 THEN use shift value from register ELSE use shift value from Imm5
  //   Buffer flags for next instruction
  //   Add 3 to offset because ARM pre-increments PC
  //   and does an additionnal prefect operation
endmodule

module Conditional (
  input  [15:0] Instruction,
  input  N,
  input  Z,
  input  C,
  input  Enable,
  input  V,
  output [7:0] Offset,
  output Verified
);

  wire and_1_out, and_2_out, and_3_out, multiplexer_1_out, not_1_out, not_2_out, not_3_out, not_4_out,
       not_5_out, not_6_out, not_7_out, not_8_out, or_1_out, xor_1_out, xor_2_out;

  not not_1 (not_1_out, Z);
  not not_2 (not_2_out, C);
  and and_1 (and_1_out, C, not_1_out);
  and and_2 (and_2_out, not_2_out, Z);
  xor xor_1 (xor_1_out, N, V);
  xor xor_2 (xor_2_out, Z, V);
  not not_3 (not_3_out, xor_1_out);
  not not_4 (not_4_out, Z);
  and and_3 (and_3_out, not_3_out, not_4_out);
  or or_1 (or_1_out, xor_2_out, Z);
  not not_5 (not_5_out, N);
  not not_6 (not_6_out, Z);
  not not_7 (not_7_out, C);
  not not_8 (not_8_out, V);
  Multiplexer #(.select(4), .enable("false")) multiplexer_1 (
    .in0(N), .in1(not_5_out), .in2(Z), .in3(not_6_out), .in4(C), .in5(not_7_out), .in6(V), .in7(not_8_out),
    .in8(and_1_out), .in9(and_2_out), .in10(xor_1_out), .in11(not_3_out), .in12(and_3_out), .in13(and_3_out),
    .in14(or_1_out), .out(multiplexer_1_out), .sel(Instruction[11:8]));  // open: in15
  and and_4 (Verified, Enable, multiplexer_1_out);

  assign Offset = Instruction[7:0];
endmodule

module Opcode_Decoder (
  input  [5:0] Opcode,
  output Data_Processing,
  output Shift,
  output Load_Store,
  output SP_Address,
  output Conditional
);

  wire not_1_out, not_2_out, not_3_out, not_4_out, not_5_out, not_6_out;

  not not_1 (not_1_out, Opcode[0]);
  not not_2 (not_2_out, Opcode[1]);
  not not_3 (not_3_out, Opcode[2]);
  not not_4 (not_4_out, Opcode[3]);
  not not_5 (not_5_out, Opcode[5]);
  not not_6 (not_6_out, Opcode[4]);
  and and_1 (Data_Processing, not_1_out, not_2_out, not_3_out, not_4_out, Opcode[4], not_5_out);
  and and_2 (Shift, not_6_out, not_5_out);
  and and_3 (Load_Store, Opcode[5], not_6_out, not_4_out, Opcode[2]);
  and and_4 (SP_Address, Opcode[5], not_6_out, Opcode[3], Opcode[2]);
  and and_5 (Conditional, Opcode[5], Opcode[4], not_4_out, Opcode[2]);

  // Notes on the sheet:
  //   Shift, add, sub, mov
  //   Load/Store
  //   SP Address
  //   Conditional branch
  //   Data Processing
endmodule

module Data_Processing (
  input  [15:0] Instruction,
  input  Enable,
  output [2:0] Rn,
  output [2:0] Rd,
  output [2:0] Rm,
  output [3:0] ALU_Opcode,
  output [3:0] Flags_Update_Mask
);

  wire [15:0] bit_extender_1_out;
  wire [15:10] and_1_out;

  assign bit_extender_1_out = {{15{1'b0}}, Enable};  // Bit_Extender bit_extender_1
  assign {and_1_out, ALU_Opcode, Rm, Rd} = Instruction & bit_extender_1_out;  // AND_Gate and_1, 16 bits wide
  Multiplexer #(.select(4), .width(4), .enable("false")) multiplexer_1 (
    .in0(4'b1110), .in1(4'b1110), .in2(4'b1110), .in3(4'b1110), .in4(4'b1110), .in5(4'b1111), .in6(4'b1111),
    .in7(4'b1110), .in8(4'b1110), .in9(4'b1111), .in10(4'b1111), .in11(4'b1111), .in12(4'b1110),
    .in13(4'b1100), .in14(4'b1110), .in15(4'b1110), .out(Flags_Update_Mask), .sel(ALU_Opcode));

  assign Rn = Rd;

  // Notes on the sheet:
  //   Note 2: RSB instruction has Rn as 1st operand.
  //   Pull output low on Enable = 0
  //   MUL instruction has Rn as 1st operand and Rdm as 2nd operand
  //   For simplification purposes, Rm is used for 1st operand both here and in the ALU.
  //   Note: instructions that does not save the result will still have the second operand as the destination register, the ALU will copy the second register to the destination register
endmodule

module Shift_Add_Sub_Mov (
  input  [15:0] Instruction,
  input  Enable,
  output [3:0] ALU_Opcode,
  output [3:0] Flags_Update_Mask,
  output Carry,
  output Imm32_Enable,
  output [2:0] Rm,
  output [2:0] Rn,
  output [2:0] Rd,
  output [4:0] Imm5,
  output [31:0] Imm32
);

  wire ADDS, ADDS_IMM, and_1_out, ASR, LSL, LSR, MOV, not_1_out, not_2_out, not_3_out, not_4_out, not_5_out,
       not_6_out, not_7_out, not_8_out, SUBS, SUBS_IMM;
  wire [2:0] IMM3, priority_encoder_1_out;
  wire [4:3] IMM5_t;
  wire [15:11] multiplexer_1_out;
  wire [31:0] bit_extender_1_out, bit_extender_2_out, IMM32_t;

  Multiplexer #(.width(16)) multiplexer_1 (
    .in1(Instruction), .out({multiplexer_1_out, IMM5_t, IMM3, Rn, Rd}), .sel(1'b0), .en(Enable));  // open: in0
  not not_1 (not_1_out, multiplexer_1_out[12]);
  not not_2 (not_2_out, multiplexer_1_out[11]);
  not not_3 (not_3_out, multiplexer_1_out[12]);
  not not_4 (not_4_out, multiplexer_1_out[11]);
  and and_1 (and_1_out, multiplexer_1_out[11], multiplexer_1_out[12]);
  and and_2 (LSL, not_1_out, not_2_out);
  and and_3 (LSR, multiplexer_1_out[11], not_3_out);
  and and_4 (ASR, not_4_out, multiplexer_1_out[12]);
  not not_5 (not_5_out, IMM5_t[3]);
  not not_6 (not_6_out, IMM5_t[4]);
  not not_7 (not_7_out, IMM5_t[4]);
  not not_8 (not_8_out, IMM5_t[3]);
  BitSelector #(.width(3)) bitselector_1 (.in(multiplexer_1_out[15:13]), .out(MOV), .sel(2'b00));
  and and_5 (ADDS, and_1_out, not_5_out, not_6_out);
  and and_6 (SUBS, and_1_out, IMM5_t[3], not_7_out);
  and and_7 (ADDS_IMM, and_1_out, not_8_out, IMM5_t[4]);
  and and_8 (SUBS_IMM, and_1_out, IMM5_t[3], IMM5_t[4]);
  or or_1 (Carry, SUBS, SUBS_IMM);
  or or_2 (Imm32_Enable, SUBS_IMM, ADDS_IMM, MOV);
  Priority_Encoder priority_encoder_1 (
    .in0(LSL), .in1(LSR), .in2(ASR), .in3(ADDS), .in4(SUBS), .in5(ADDS_IMM), .in6(SUBS_IMM), .in7(MOV),
    .out(priority_encoder_1_out), .en_in(1'b1));  // open: gs, en_out
  assign bit_extender_1_out = {{29{1'b0}}, IMM3};  // Bit_Extender bit_extender_1
  assign bit_extender_2_out = {{24{1'b0}}, {IMM3[1:0], Rn, Rd}};  // Bit_Extender bit_extender_2
  Multiplexer #(.select(3), .width(4), .enable("false")) multiplexer_2 (
    .in0(4'b0000), .in1(4'b0001), .in2(4'b0010), .in3(4'b0011), .in4(4'b0100), .in5(4'b0101), .in6(4'b0110),
    .in7(4'b0111), .out(ALU_Opcode), .sel(priority_encoder_1_out));
  Multiplexer #(.select(3), .width(4), .enable("false")) multiplexer_3 (
    .in0(4'b1110), .in1(4'b1110), .in2(4'b1110), .in3(4'b1111), .in4(4'b1111), .in5(4'b1111), .in6(4'b1111),
    .in7(4'b1100), .out(Flags_Update_Mask), .sel(priority_encoder_1_out));
  Multiplexer #(.select(3), .width(3), .enable("false")) multiplexer_4 (
    .in0(Rn), .in1(Rn), .in2(Rn), .in3(IMM3), .in4(IMM3), .in5(3'b000), .in6(3'b000), .in7(3'b000), .out(Rm),
    .sel(priority_encoder_1_out));
  Multiplexer #(.select(3), .width(32), .enable("false")) multiplexer_5 (
    .in0({32{1'b0}}), .in1({32{1'b0}}), .in2({32{1'b0}}), .in3(bit_extender_1_out), .in4(bit_extender_1_out),
    .in5({32{1'b0}}), .in6({32{1'b0}}), .in7(bit_extender_2_out), .out(IMM32_t), .sel(priority_encoder_1_out));

  // Other names for the same wires on the sheet: IMM8[7:0] = {IMM3[1:0], Rn, Rd}; RMA[2:0] = Rn; IMM5_t[2:0] = IMM3;
  //   RMB[2:0] = IMM3; ENABLE_IMM32 = Imm32_Enable; FLAGS[3:0] = Flags_Update_Mask

  // Notes on the sheet:
  //   Pull output low on Enable = 0
  //   Note: ALU uses Rn register for shifts. Use Rn instead of Rm for shifts (immediate) here too
  //   Note 2: MOV uses RSB ALU opcode with Imm8 reversed so that it is copied to output register
  //   Note 3: Imm32_Enable forces the use of the immediate for Rm register
  //   Enable carry for SUB since it is reversed in ALU
  //   ALU will use Imm32 instead of Rm
endmodule

module Load_Store (
  input  Enable,
  input  [15:0] Instruction,
  input  Clk,
  input  Reset,
  input  [31:0] Stack_Pointer,
  output Store,
  output Load,
  output PC_Hold,
  output [2:0] Rm,
  output [2:0] Rd,
  output [31:0] RAM_Addr
);

  wire d_ff_1_q, not_1_out, xor_1_out;
  wire [2:0] bit_extender_2_out, bit_extender_3_out;
  wire [31:0] adder_1_out, bit_extender_1_out, bit_extender_4_out;

  xor xor_1 (xor_1_out, Instruction[11], d_ff_1_q);
  D_Flip_Flop d_ff_1 (.D(xor_1_out), .clk(Clk), .Q(d_ff_1_q), .preset(1'b0), .reset(Reset));  // open: Qn
  not not_1 (not_1_out, Instruction[11]);
  assign bit_extender_1_out = {{24{Instruction[7]}}, Instruction[7:0]};  // Bit_Extender bit_extender_1
  Adder #(.width(32)) adder_1 (.a(bit_extender_1_out), .b(Stack_Pointer), .out(adder_1_out));  // open: cin, cout
  and and_1 (Store, Enable, not_1_out);
  and and_2 (Load, Enable, Instruction[11]);
  and and_3 (PC_Hold, Enable, d_ff_1_q);
  assign bit_extender_2_out = {{2{Enable}}, Enable};  // Bit_Extender bit_extender_2
  assign bit_extender_3_out = {{2{Enable}}, Enable};  // Bit_Extender bit_extender_3
  assign bit_extender_4_out = {{31{Enable}}, Enable};  // Bit_Extender bit_extender_4
  assign Rm = Instruction[10:8] & bit_extender_2_out;  // AND_Gate and_4, 3 bits wide
  assign Rd = Instruction[10:8] & bit_extender_3_out;  // AND_Gate and_5, 3 bits wide
  assign RAM_Addr = adder_1_out & bit_extender_4_out;  // AND_Gate and_6, 32 bits wide

  // Notes on the sheet:
  //   Delay load and hold PC for 1 cycle for the RAM to send out requested data 
endmodule

module SP_Address (
  input  Enable,
  input  [15:0] Instruction,
  input  [31:0] Stack_Pointer,
  output [31:0] New_Stack_Pointer,
  output Write_Enable
);

  wire adder_1_cout, and_1_out, and_2_out, BIT_7_1, nor_1_out, priority_encoder_1_out, subtractor_1_bout;
  wire [31:0] adder_1_out, IMM7_32, subtractor_1_out;

  not not_1 (BIT_7_1, Instruction[7]);
  assign IMM7_32 = {{25{1'b0}}, Instruction[6:0]};  // Bit_Extender bit_extender_1
  Adder #(.width(32)) adder_1 (.a(IMM7_32), .b(Stack_Pointer), .out(adder_1_out), .cout(adder_1_cout));  // open: cin
  Subtractor #(.width(32)) subtractor_1 (
    .a(IMM7_32), .b(Stack_Pointer), .out(subtractor_1_out), .bout(subtractor_1_bout));  // open: bin
  Priority_Encoder #(.select(1)) priority_encoder_1 (
    .in0(BIT_7_1), .in1(Instruction[7]), .out(priority_encoder_1_out));  // open: gs, en_out, en_in
  and and_1 (and_1_out, subtractor_1_bout, Instruction[7]);
  and and_2 (and_2_out, adder_1_cout, BIT_7_1);
  Multiplexer #(.width(32)) multiplexer_1 (
    .in0(adder_1_out), .in1(subtractor_1_out), .out(New_Stack_Pointer), .sel(priority_encoder_1_out),
    .en(Enable));
  nor nor_1 (nor_1_out, and_1_out, and_2_out);
  and and_3 (Write_Enable, nor_1_out, Enable);

  // Other names for the same wires on the sheet: BIT_7_0 = Instruction[7]; SP[31:0] = Stack_Pointer

  // Notes on the sheet:
  //   Pull output low on Enable = 0
endmodule

module Flags_APSR (
  input  [3:0] Flags_In,
  input  [3:0] Update_Mask,
  input  Clk,
  input  Rst,
  output [3:0] Flags_Out
);

  Register #(.width(1)) register_1 (.D(Flags_In[0]), .en(Update_Mask[0]), .clk(Clk), .Q(Flags_Out[0]), .clr(Rst));
  Register #(.width(1)) register_2 (.D(Flags_In[1]), .en(Update_Mask[1]), .clk(Clk), .Q(Flags_Out[1]), .clr(Rst));
  Register #(.width(1)) register_3 (.D(Flags_In[2]), .en(Update_Mask[2]), .clk(Clk), .Q(Flags_Out[2]), .clr(Rst));
  Register #(.width(1)) register_4 (.D(Flags_In[3]), .en(Update_Mask[3]), .clk(Clk), .Q(Flags_Out[3]), .clr(Rst));
endmodule
