// Logisim project Machine.circ as structural Verilog: 2 circuits, main circuit main
module main (
  input  GPIO_A1,
  input  GPIO_A3,
  input  GPIO_A5,
  input  GPIO_A7,
  input  GPIO_A9,
  input  GPIO_A11,
  input  GPIO_A13,
  input  GPIO_A15,
  input  GPIO_A17,
  input  GPIO_A19,
  input  GPIO_A21,
  input  GPIO_A23,
  input  GPIO_A25,
  input  GPIO_A27,
  input  GPIO_A29,
  input  GPIO_A31,
  input  GPIO_A33,
  input  GPIO_A35,
  input  GPIO_B1,
  input  GPIO_B3,
  input  GPIO_B5,
  input  GPIO_B7,
  input  GPIO_B9,
  input  GPIO_B11,
  input  GPIO_B13,
  input  GPIO_B15,
  input  GPIO_B17,
  input  GPIO_B19,
  input  GPIO_B21,
  input  GPIO_B23,
  input  GPIO_B25,
  input  GPIO_B27,
  input  GPIO_B29,
  input  GPIO_B31,
  input  GPIO_B33,
  input  GPIO_B35,
  output GPIO_A2,
  output GPIO_A4,
  output GPIO_A6,
  output GPIO_A8,
  output GPIO_A10,
  output GPIO_A12,
  output GPIO_A14,
  output GPIO_A16,
  output GPIO_A18,
  output GPIO_A20,
  output GPIO_A22,
  output GPIO_A24,
  output GPIO_A26,
  output GPIO_A28,
  output GPIO_A30,
  output GPIO_A32,
  output GPIO_A34,
  output GPIO_A36,
  output GPIO_B2,
  output GPIO_B4,
  output GPIO_B6,
  output GPIO_B8,
  output GPIO_B10,
  output GPIO_B12,
  output GPIO_B14,
  output GPIO_B16,
  output GPIO_B18,
  output GPIO_B20,
  output GPIO_B22,
  output GPIO_B24,
  output GPIO_B26,
  output GPIO_B28,
  output GPIO_B30,
  output GPIO_B32,
  output GPIO_B34,
  output GPIO_B36
);

  wire Clk_Button_out, clock_1_out, CPU_1_p6, CPU_1_p7, CPU_1_p8, CPU_1_p9, CPU_1_p10, CPU_1_p11, CPU_1_p12,
       CPU_1_p16, Rst_Button_out;
  wire [7:0] RAM_Addr, ROM_Addr;
  wire [15:0] ROMa_data;
  wire [31:0] CPU_1_p5, CPU_1_p15, RAMa_dout;
  wire [31:8] CPU_1_p14;

  RAM #(.dataWidth(32), .databus("bibus")) RAMa (
    .addr(RAM_Addr), .we(CPU_1_p16), .oe(1'b1), .clk(clock_1_out), .din(CPU_1_p15), .dout(RAMa_dout));
  Clock clock_1 (.out(clock_1_out));
  LED A0 (.in(RAMa_dout[0]));
  LED A1 (.in(RAMa_dout[1]));
  LED A2 (.in(RAMa_dout[2]));
  ROM #(.dataWidth(16)) ROMa (.addr(ROM_Addr), .data(ROMa_data));
  Button Clk_Button (.out(Clk_Button_out));
  Button Rst_Button (.out(Rst_Button_out));
  LED A3 (.in(RAMa_dout[3]));
  LED A4 (.in(RAMa_dout[4]));
  LED A5 (.in(RAMa_dout[5]));
  LED A6 (.in(RAMa_dout[6]));
  LED A7 (.in(RAMa_dout[7]));
  LED L0 (.in(CPU_1_p5[0]));
  // Probe on CPU_1_p6
  // Probe on CPU_1_p5
  LED L3 (.in(CPU_1_p5[3]));
  LED L1 (.in(CPU_1_p5[1]));
  LED L2 (.in(CPU_1_p5[2]));
  // Probe on CPU_1_p8
  // Probe on CPU_1_p7
  // Probe on CPU_1_p10
  // Probe on CPU_1_p9
  LED L4 (.in(CPU_1_p5[4]));
  LED L5 (.in(CPU_1_p5[5]));
  // Probe on CPU_1_p12
  // Probe on CPU_1_p11
  // CPU CPU_1: pin names not known; wires that end beside it: clock_1_out, Rst_Button_out, RAMa_dout, ROMa_data, CPU_1_p5, CPU_1_p6, CPU_1_p7, CPU_1_p8, CPU_1_p9, CPU_1_p10, CPU_1_p11, CPU_1_p12, ROM_Addr, {CPU_1_p14, RAM_Addr}, CPU_1_p15, CPU_1_p16
  LED L6 (.in(CPU_1_p5[6]));
  LED L7 (.in(CPU_1_p5[7]));
  LED LED_1 (.in(RAM_Addr[0]));
  LED LED_2 (.in(RAM_Addr[1]));
  LED LED_3 (.in(RAM_Addr[2]));
  LED LED_4 (.in(RAM_Addr[3]));
  LED LED_5 (.in(RAM_Addr[4]));
  LED LED_6 (.in(RAM_Addr[5]));
  LED LED_7 (.in(RAM_Addr[6]));
  LED LED_8 (.in(RAM_Addr[7]));

  // Notes on the sheet:
  //   contents of ROMa (hex, n*v repeats v):
  //   b08c 2000 9008 21ff 9104 9000 defe 9800 9904 4288 da08 defe 9800 9908 4081 9108 defe 9800 1c40 9000
  //   def0 b00c
  //   Use only 8 bit adresses
  //   VCC 5V
  //   VCC 3.3V
  //   VCC 5V
  //   VCC 3.3V
  //   GROUND
  //   GROUND
  //   GROUND
  //   GROUND
endmodule

module CPU (
  input  [31:0] RAM_In,
  input  [15:0] ROM_In,
  input  Clk,
  input  Reset,
  output [7:0] ROM_Addr,
  output [31:0] R3,
  output [31:0] R7,
  output [31:0] R2,
  output [31:0] R6,
  output [31:0] RAM_Addr,
  output [31:0] R1,
  output [31:0] R5,
  output [31:0] R0,
  output [31:0] R4,
  output [31:0] RAM_Out,
  output Store
);

  wire CARRY, DP_SHIFT, IMM32_EN, LOAD;
  wire [2:0] REG_DEST, Rm, Rn;
  wire [3:0] ALU_Opcode, FLAGS;
  wire [4:0] IMM5, multiplexer_1_out;
  wire [31:0] A_Rn, B_Rm, IMM32, multiplexer_3_out, RAM_Addr_t;

  Controller Controller_1 (
    .Inst(ROM_In), .Rm(Rm), .PC(ROM_Addr), .ALU_Opcode(ALU_Opcode), .Imm5(IMM5), .Rn(Rn), .Flags(FLAGS),
    .Imm32_Enable(IMM32_EN), .Rd(REG_DEST), .Imm32(IMM32), .DP_Shift(DP_SHIFT), .Carry(CARRY),
    .RAM_Addr(RAM_Addr_t), .Load(LOAD), .Store(Store), .Clk(Clk), .Reset(Reset));
  Multiplexer #(.width(5), .enable("false")) multiplexer_1 (
    .in0(IMM5), .in1(B_Rm[4:0]), .out(multiplexer_1_out), .sel(DP_SHIFT));
  // BancRegistre Regs_1: pin names not known; wires that end beside it: RAM_In, REG_DEST, Clk, R0, Reset, R1, R2, R3, R4, Rn, R5, R6, Rm, R7, B_Rm, A_Rn
  ALU ALU_1 (
    .S(RAM_In), .Flags(FLAGS), .A(A_Rn), .B(multiplexer_3_out), .Shift(multiplexer_1_out), .CarryIn(CARRY),
    .Codop(ALU_Opcode));
  Multiplexer #(.width(32), .enable("false")) multiplexer_2 (
    .in1(RAM_Addr_t), .out(RAM_Addr), .sel(LOAD));  // open: in0
  Multiplexer #(.width(32), .enable("false")) multiplexer_3 (
    .in0(B_Rm), .in1(IMM32), .out(multiplexer_3_out), .sel(IMM32_EN));

  assign RAM_Out = RAM_In;

  // Other names for the same wires on the sheet: ALU_RESULT[31:0] = RAM_In; PC[7:0] = ROM_Addr
endmodule
